# Fritzing sketch example_hookup (saved by Fritzing 0.9.2b)
breadboards: 1

parts:
  Part2 = Breadboard Power Supply Board SMD
  Part3 = FTDI Basic Programmer
  Part4 = ESP32 Module Testbed
  S1 = Pushbutton [package="[THT]"]
  S2 = Toggle Switch [package=THT]
  R1 = Resistor [tolerance=±5% resistance=10k package=THT]
  R2 = Resistor [tolerance=±5% resistance=10k package=THT]
  LED1 = LED - 5mm [color="Red (633nm)" package="5 mm [THT]"]
  R3 = Resistor [tolerance=±5% resistance=330 package=THT]
  U1 = LIPO-1000mAh [package=lipo-1000]

nets:
  GND: Part2.GND, Part3.GND, Part4.GND, S1.Pin_3, S1.Pin_4, S2.L2, LED1.cathode, U1.-
  3.3V: Part2.VCC, Part4.3V3, R1.Pin_0, R2.Pin_0
  N1: Part2.VIN, U1.+
  N2: Part3.RXI, Part4.TXD0
  N3: Part3.TXO, Part4.RXD0
  N4: Part4.EN, S1.Pin_1, S1.Pin_2, R2.Pin_1
  N5: Part4.IO0, S2.COM
  N6: Part4.IO16, R3.Pin_0
  N7: S2.L1, R1.Pin_1
  N8: LED1.anode, R3.Pin_1

custom parts:
  ESP32 Module Testbed: The ESP32 Module Testbed is a breadboard compatible breakout board for the ESP-WROOM-03 ESP32 module. The ESP32 is a WiFi and Bluetooth-enabled 32-bit, dual-core microcontroller.
